// Logisim project 2s comp.circ as structural Verilog: 1 circuit, main circuit main
module main (
  input  B0,
  input  B1,
  input  B2,
  input  B3,
  input  ADD_SUB,
  input  A0,
  input  A1,
  input  A2,
  input  A3,
  output C0,
  output C1,
  output C2,
  output C3,
  output out_14,
  output out_15
);

  wire adder_2_cout, adder_3_cout, adder_4_cout, xor_1_out, xor_2_out, xor_3_out, xor_4_out;

  xor xor_1 (xor_1_out, ADD_SUB, B2);
  xor xor_2 (xor_2_out, ADD_SUB, B3);
  Adder #(.width(1)) adder_1 (.a(xor_2_out), .b(A3), .out(C3), .cin(adder_2_cout), .cout(out_14));
  xor xor_3 (xor_3_out, B1, ADD_SUB);
  Adder #(.width(1)) adder_2 (.a(xor_1_out), .b(A1), .out(C2), .cin(adder_4_cout), .cout(adder_2_cout));
  xor xor_4 (xor_4_out, B0, ADD_SUB);
  Adder #(.width(1)) adder_3 (.a(xor_4_out), .b(A0), .out(C0), .cin(ADD_SUB), .cout(adder_3_cout));
  Adder #(.width(1)) adder_4 (.a(xor_3_out), .b(A1), .out(C1), .cin(adder_3_cout), .cout(adder_4_cout));
  xor xor_5 (out_15, adder_2_cout, out_14);

  assign A2 = A1;

  // Notes on the sheet:
  //                       CARRY OUT
  //                      OVERFLOW
  //                                    2'S COMPLEMENT ADDITION \ SUBTRACTION
endmodule
