// Logisim project ALU FOR NISUMANO.circ as structural Verilog: 1 circuit, main circuit main
module main (
  input  ENABLE_ALU,
  input  [2:0] in_2,
  input  [15:0] DRAIN,
  input  [15:0] SOURCE,
  input  [15:0] CONSTANT,
  output ALU_FKT,
  output [15:0] OUT,
  output CARRY_OUT,
  output BORROW_OUT
);

  wire adder_1_cout, adder_2_cout, demultiplexer_1_out0, demultiplexer_1_out1, demultiplexer_1_out2,
       demultiplexer_1_out3, demultiplexer_1_out4, demultiplexer_1_out5, demultiplexer_1_out6,
       demultiplexer_1_out7, subtractor_1_bout, subtractor_2_bout;
  wire [15:0] adder_1_out, adder_2_out, divider_1_out, multiplier_1_out, nand_1_out, not_1_out,
       pull_resistor_4_node, pull_resistor_5_node, pull_resistor_6_node, pull_resistor_7_node,
       pull_resistor_8_node, pull_resistor_9_node, pull_resistor_10_node, pull_resistor_11_node,
       pull_resistor_12_node, pull_resistor_13_node, pull_resistor_14_node, subtractor_1_out,
       subtractor_2_out;

  Demultiplexer #(.select(3)) demultiplexer_1 (
    .out0(demultiplexer_1_out0), .out1(demultiplexer_1_out1), .out2(demultiplexer_1_out2),
    .out3(demultiplexer_1_out3), .out4(demultiplexer_1_out4), .out5(demultiplexer_1_out5),
    .out6(demultiplexer_1_out6), .out7(demultiplexer_1_out7), .in(ENABLE_ALU), .sel(in_2));  // open: en
  or or_1 (ALU_FKT, demultiplexer_1_out0, demultiplexer_1_out1, demultiplexer_1_out2, demultiplexer_1_out3, demultiplexer_1_out4, demultiplexer_1_out5, demultiplexer_1_out6, demultiplexer_1_out7);
  Pull_Resistor pull_resistor_1 (.node(DRAIN));
  Pull_Resistor pull_resistor_2 (.node(SOURCE));
  Pull_Resistor pull_resistor_3 (.node(CONSTANT));
  Pull_Resistor pull_resistor_4 (.node(pull_resistor_4_node));
  assign pull_resistor_4_node = demultiplexer_1_out7 ? adder_1_out : 16'bz;  // Controlled_Buffer controlled_buffer_1
  Adder #(.width(16)) adder_1 (.a(DRAIN), .b(SOURCE), .out(adder_1_out), .cout(adder_1_cout));  // open: cin
  Adder #(.width(16)) adder_2 (.a(DRAIN), .b(CONSTANT), .out(adder_2_out), .cout(adder_2_cout));  // open: cin
  Subtractor #(.width(16)) subtractor_1 (
    .a(DRAIN), .b(SOURCE), .out(subtractor_1_out), .bout(subtractor_1_bout));  // open: bin
  Subtractor #(.width(16)) subtractor_2 (
    .a(DRAIN), .b(CONSTANT), .out(subtractor_2_out), .bout(subtractor_2_bout));  // open: bin
  Multiplier #(.width(16)) multiplier_1 (.a(DRAIN), .b(SOURCE), .out(multiplier_1_out));  // open: cin, cout
  Divider #(.width(16)) divider_1 (.a(DRAIN), .b(SOURCE), .out(divider_1_out));  // open: upper, rem
  assign nand_1_out = ~(DRAIN & SOURCE);  // NAND_Gate nand_1, 16 bits wide
  assign not_1_out = ~DRAIN;  // NOT_Gate not_1, 16 bits wide
  Pull_Resistor pull_resistor_5 (.node(pull_resistor_5_node));
  Pull_Resistor pull_resistor_6 (.node(pull_resistor_6_node));
  Pull_Resistor pull_resistor_7 (.node(pull_resistor_7_node));
  assign pull_resistor_7_node = demultiplexer_1_out4 ? subtractor_2_out : 16'bz;  // Controlled_Buffer controlled_buffer_2
  assign pull_resistor_6_node = demultiplexer_1_out5 ? subtractor_1_out : 16'bz;  // Controlled_Buffer controlled_buffer_3
  assign pull_resistor_5_node = demultiplexer_1_out6 ? adder_2_out : 16'bz;  // Controlled_Buffer controlled_buffer_4
  assign OUT = pull_resistor_4_node | pull_resistor_5_node | pull_resistor_6_node | pull_resistor_7_node | pull_resistor_8_node | pull_resistor_9_node | pull_resistor_12_node | pull_resistor_11_node | pull_resistor_10_node | pull_resistor_14_node | pull_resistor_13_node;  // OR_Gate or_2, 16 bits wide
  Pull_Resistor pull_resistor_8 (.node(pull_resistor_8_node));
  Pull_Resistor pull_resistor_9 (.node(pull_resistor_9_node));
  assign pull_resistor_9_node = demultiplexer_1_out2 ? divider_1_out : 16'bz;  // Controlled_Buffer controlled_buffer_5
  assign pull_resistor_8_node = demultiplexer_1_out3 ? multiplier_1_out : 16'bz;  // Controlled_Buffer controlled_buffer_6
  Pull_Resistor pull_resistor_10 (.node(pull_resistor_10_node));
  assign pull_resistor_10_node = demultiplexer_1_out0 ? not_1_out : 16'bz;  // Controlled_Buffer controlled_buffer_7
  Pull_Resistor pull_resistor_11 (.node(pull_resistor_11_node));
  Pull_Resistor pull_resistor_12 (.node(pull_resistor_12_node));
  assign pull_resistor_11_node = demultiplexer_1_out1 ? nand_1_out : 16'bz;  // Controlled_Buffer controlled_buffer_8
  Pull_Resistor pull_resistor_13 (.node(pull_resistor_13_node));
  Pull_Resistor pull_resistor_14 (.node(pull_resistor_14_node));
  or or_3 (CARRY_OUT, adder_1_cout, adder_2_cout);
  or or_4 (BORROW_OUT, subtractor_1_bout, subtractor_2_bout);

  // Notes on the sheet:
  //   TO INPR
  //   16 BIT ALU
  //   TO AC
  //   OPCODE   FOR  OPERATION
  //   NOT   0
  //   NAND   1
  //   DIV  2
  //   MUL  3
  //   SUC  4
  //   SUB  5
  //   ADC  6
  //   ADD  7
  //   NOT
  //   NAND
  //   DIV
  //   MUL
  //   SUC
  //   SUB
  //   ADC
  //   ADD
  //   ALU ON\OFF INDICATOR
  //   TO AC
  //              TO FLIPFLOP E
endmodule
