// Logisim project Load and Store.circ as structural Verilog: 1 circuit, main circuit main
module main (
  input  in_1
);

  wire clock_1_out, not_1_out;
  wire [15:0] ram_1_data, register_1_q, register_2_q;

  Register #(.width(16)) register_1 (.Q(register_1_q), .clk(clock_1_out));  // open: D, en, clr
  RAM #(.addrWidth(16), .dataWidth(16), .bus("separate")) ram_1 (
    .addr(register_2_q), .din(register_1_q), .data(ram_1_data), .str(not_1_out), .clk(clock_1_out), .ld(in_1));  // open: sel, clr
  Register #(.width(16)) register_2 (.Q(register_2_q), .clk(clock_1_out));  // open: D, en, clr
  Clock clock_1 (.out(clock_1_out));
  not not_1 (not_1_out, in_1);
  Register #(.width(16)) register_3 (.D(ram_1_data), .clk(clock_1_out));  // open: en, Q, clr

  // Notes on the sheet:
  //   load and store
  //   DR
  //               memory
  //   AR
  //                              output register
endmodule
