// Logisim project NISUMANO.circ as structural Verilog: 1 circuit, main circuit main
// AR
module main (
  input  in_1,
  input  [2:0] in_2,
  input  [15:0] DRAIN,
  input  [15:0] SOURCE,
  input  [15:0] CONSTANT,
  input  [2:0] in_6,
  input  in_7,
  input  in_8,
  input  in_9,
  input  [15:0] in_10,
  input  [2:0] in_11,
  input  in_12,
  input  [15:0] in_13,
  input  [15:0] in_14,
  input  in_15,
  input  [7:0] in_16,
  input  [15:0] in_17,
  input  [1:0] in_18,
  input  [15:0] in_19,
  input  [15:0] in_20,
  input  [3:0] in_21,
  input  in_22,
  input  in_23,
  input  [15:0] in_24,
  output ALU_FKT,
  output [15:0] OUT,
  output CARRY_OUT,
  output BORROW_OUT,
  output [15:0] out_29,
  output [15:0] out_30,
  output [1:0] out_31
);

  wire ADD_out, adder_3_cout, adder_4_cout, AND_out, clock_1_out, clock_2_out, clock_3_out, clock_4_out,
       CLR_out, COM_out, demultiplexer_1_out0, demultiplexer_1_out1, demultiplexer_1_out2,
       demultiplexer_1_out3, demultiplexer_1_out4, demultiplexer_1_out5, demultiplexer_1_out6,
       demultiplexer_1_out7, DR_2_out, INC_out, INPR_2_out, not_2_out, or_3_out, SHL_out, SHR_out,
       subtractor_1_bout, subtractor_2_bout, undriven_4, undriven_5, undriven_6, undriven_7, undriven_8,
       undriven_9, undriven_10, undriven_11, undriven_12, undriven_13, undriven_14, undriven_15, undriven_16,
       undriven_17, undriven_18, undriven_19, undriven_20, undriven_21, undriven_22, undriven_25,
       undriven_26, undriven_27, undriven_28, undriven_29;
  wire [7:0] bit_extender_3_out, undriven, undriven_23;
  wire [11:0] AR_3_q, bit_extender_1_out, bit_extender_2_out, PC_2_q;
  wire [15:0] adder_1_out, adder_2_out, adder_3_out, adder_4_out, AR_2_q, AR_q, counter_1_q, divider_1_out,
       DR_3_q, multiplier_1_out, nand_1_out, not_1_out, OUTR_3_q, pull_resistor_4_node, pull_resistor_5_node,
       pull_resistor_6_node, pull_resistor_7_node, pull_resistor_8_node, pull_resistor_9_node,
       pull_resistor_10_node, pull_resistor_11_node, pull_resistor_12_node, pull_resistor_13_node,
       pull_resistor_14_node, subtractor_1_out, subtractor_2_out, undriven_2, undriven_3, undriven_24;

  RAM #(.addrWidth(16), .dataWidth(16), .bus("separate")) ram_1 (
    .addr(AR_q), .data(out_29), .ld(in_12));  // open: din, str, sel, clk, clr
  Register #(.width(16)) AR (.D(in_13), .Q(AR_q));  // open: en, clk, clr
  Register #(.width(16)) AR_2 (.D(AR_2_q), .Q(AR_2_q), .clk(clock_1_out));  // open: en, clr
  Register #(.width(16)) PC (.D(AR_2_q), .Q(AR_2_q), .clk(clock_1_out));  // open: en, clr
  Register #(.width(16)) DR (.D(AR_2_q), .Q(AR_2_q), .clk(clock_1_out));  // open: en, clr
  Register #(.width(16)) AC (.D(undriven_2), .Q(AR_2_q), .clk(clock_1_out));  // open: en, clr
  Register INPR (.D(undriven));  // open: en, Q, clk, clr
  Register #(.width(16)) IR (.D(AR_2_q), .Q(AR_2_q), .clk(clock_1_out));  // open: en, clr
  Register #(.width(16)) TR (.D(AR_2_q), .Q(AR_2_q), .clk(clock_1_out));  // open: en, clr
  Register #(.width(16)) OUTR (.D(AR_2_q), .clk(clock_1_out));  // open: en, Q, clr
  RAM #(.addrWidth(16), .dataWidth(16)) ram_2 (.addr(AR_2_q), .data(AR_2_q));  // open: sel, clk, ld, clr
  Clock clock_1 (.out(clock_1_out));
  Multiplexer #(.select(3), .width(16)) multiplexer_1 (.out(AR_2_q));  // open: in0, in1, in2, in3, in4, in5, in6, in7, sel, en
  ROM rom_1 ();  // open: addr, data, sel
  Counter #(.width(16), .max('hffff)) counter_1 (
    .Q(counter_1_q), .clk(clock_2_out));  // open: load, D, count, carry, clr
  Adder #(.width(16)) adder_1 (.a(in_14), .b(in_17), .out(adder_1_out));  // open: cin, cout
  Multiplexer #(.select(4), .width(16)) multiplexer_2 (
    .in1(in_20), .in6(in_20), .in12(undriven_3), .in13(undriven_3), .in14(undriven_3), .in15(undriven_3),
    .out(in_20));  // open: in0, in2, in3, in4, in5, in7, in8, in9, in10, in11, sel, en
  Clock clock_2 (.out(clock_2_out));
  Register #(.width(16)) OUTR_2 (.D(adder_1_out), .en(in_15), .clk(clock_3_out));  // open: Q, clr
  Clock #(.highDuration(5)) clock_3 (.out(clock_3_out));
  Register #(.width(16)) OUTR_3 (.D(counter_1_q), .en(in_22), .Q(OUTR_3_q), .clk(clock_2_out));  // open: clr
  Adder #(.width(16)) adder_2 (.a(OUTR_3_q), .b(in_24), .out(adder_2_out));  // open: cin, cout
  Register #(.width(16)) IR_2 (.D(in_19), .Q(in_20), .clr(undriven_4));  // open: en, clk
  Register #(.width(16)) OUTR_4 (.D(adder_2_out), .en(in_23), .clk(clock_2_out));  // open: Q, clr
  Demultiplexer #(.select(3)) demultiplexer_1 (
    .out0(demultiplexer_1_out0), .out1(demultiplexer_1_out1), .out2(demultiplexer_1_out2),
    .out3(demultiplexer_1_out3), .out4(demultiplexer_1_out4), .out5(demultiplexer_1_out5),
    .out6(demultiplexer_1_out6), .out7(demultiplexer_1_out7), .in(in_1), .sel(in_2));  // open: en
  BitSelector #(.group(2)) bitselector_1 (.in(in_16), .out(out_31), .sel(in_18));
  Pull_Resistor pull_resistor_1 (.node(CONSTANT));
  or or_1 (ALU_FKT, demultiplexer_1_out0, demultiplexer_1_out1, demultiplexer_1_out2, demultiplexer_1_out3, demultiplexer_1_out4, demultiplexer_1_out5, demultiplexer_1_out6, demultiplexer_1_out7);
  Pull_Resistor pull_resistor_2 (.node(DRAIN));
  Pull_Resistor pull_resistor_3 (.node(SOURCE));
  Pull_Resistor pull_resistor_4 (.node(pull_resistor_4_node));
  assign pull_resistor_4_node = demultiplexer_1_out7 ? adder_3_out : 16'bz;  // Controlled_Buffer controlled_buffer_1
  Adder #(.width(16)) adder_3 (.a(DRAIN), .b(SOURCE), .out(adder_3_out), .cout(adder_3_cout));  // open: cin
  Adder #(.width(16)) adder_4 (.a(DRAIN), .b(CONSTANT), .out(adder_4_out), .cout(adder_4_cout));  // open: cin
  Subtractor #(.width(16)) subtractor_1 (
    .a(DRAIN), .b(SOURCE), .out(subtractor_1_out), .bout(subtractor_1_bout));  // open: bin
  Subtractor #(.width(16)) subtractor_2 (
    .a(DRAIN), .b(CONSTANT), .out(subtractor_2_out), .bout(subtractor_2_bout));  // open: bin
  Multiplier #(.width(16)) multiplier_1 (.a(DRAIN), .b(SOURCE), .out(multiplier_1_out));  // open: cin, cout
  Divider #(.width(16)) divider_1 (.a(DRAIN), .b(SOURCE), .out(divider_1_out));  // open: upper, rem
  assign nand_1_out = ~(DRAIN & SOURCE);  // NAND_Gate nand_1, 16 bits wide
  assign not_1_out = ~DRAIN;  // NOT_Gate not_1, 16 bits wide
  Pull_Resistor pull_resistor_5 (.node(pull_resistor_5_node));
  Pull_Resistor pull_resistor_6 (.node(pull_resistor_6_node));
  Pull_Resistor pull_resistor_7 (.node(pull_resistor_7_node));
  assign pull_resistor_7_node = demultiplexer_1_out4 ? subtractor_2_out : 16'bz;  // Controlled_Buffer controlled_buffer_2
  assign pull_resistor_6_node = demultiplexer_1_out5 ? subtractor_1_out : 16'bz;  // Controlled_Buffer controlled_buffer_3
  assign pull_resistor_5_node = demultiplexer_1_out6 ? adder_4_out : 16'bz;  // Controlled_Buffer controlled_buffer_4
  assign OUT = pull_resistor_4_node | pull_resistor_5_node | pull_resistor_6_node | pull_resistor_7_node | pull_resistor_8_node | pull_resistor_10_node | pull_resistor_9_node | pull_resistor_12_node | pull_resistor_11_node | pull_resistor_14_node | pull_resistor_13_node;  // OR_Gate or_2, 16 bits wide
  Pull_Resistor pull_resistor_8 (.node(pull_resistor_8_node));
  Pull_Resistor pull_resistor_9 (.node(pull_resistor_9_node));
  Pull_Resistor pull_resistor_10 (.node(pull_resistor_10_node));
  assign pull_resistor_10_node = demultiplexer_1_out2 ? divider_1_out : 16'bz;  // Controlled_Buffer controlled_buffer_5
  assign pull_resistor_8_node = demultiplexer_1_out3 ? multiplier_1_out : 16'bz;  // Controlled_Buffer controlled_buffer_6
  and AND (AND_out, undriven_5, undriven_6);
  and ADD (ADD_out, undriven_7, undriven_8);
  and DR_2 (DR_2_out, undriven_9, undriven_10);
  and INPR_2 (INPR_2_out, undriven_11, undriven_12);
  and COM (COM_out, undriven_13, undriven_14);
  and SHR (SHR_out, undriven_15, undriven_16);
  and SHL (SHL_out, undriven_17, undriven_18);
  and INC (INC_out, undriven_19, undriven_20);
  and CLR (CLR_out, undriven_21, undriven_22);
  Pull_Resistor pull_resistor_11 (.node(pull_resistor_11_node));
  Pull_Resistor pull_resistor_12 (.node(pull_resistor_12_node));
  assign pull_resistor_11_node = demultiplexer_1_out0 ? not_1_out : 16'bz;  // Controlled_Buffer controlled_buffer_7
  assign pull_resistor_12_node = demultiplexer_1_out1 ? nand_1_out : 16'bz;  // Controlled_Buffer controlled_buffer_8
  Pull_Resistor pull_resistor_13 (.node(pull_resistor_13_node));
  Pull_Resistor pull_resistor_14 (.node(pull_resistor_14_node));
  or or_3 (or_3_out, AND_out, ADD_out, DR_2_out, INPR_2_out, COM_out, SHR_out, SHL_out);
  or or_4 (CARRY_OUT, adder_3_cout, adder_4_cout);
  or or_5 (BORROW_OUT, subtractor_1_bout, subtractor_2_bout);
  not not_2 (not_2_out, in_9);
  Bit_Extender #(.in_width(16), .out_width(12)) bit_extender_1 (.in(DR_3_q), .out(bit_extender_1_out));
  Bit_Extender #(.in_width(16), .out_width(12)) bit_extender_2 (.in(DR_3_q), .out(bit_extender_2_out));
  Bit_Extender #(.in_width(16), .out_width(8)) bit_extender_3 (.in(DR_3_q), .out(bit_extender_3_out));
  Register #(.width(12)) AR_3 (.D(bit_extender_1_out), .Q(AR_3_q), .clk(clock_4_out), .clr(undriven_25));  // open: en
  Register #(.width(12)) PC_2 (.D(bit_extender_2_out), .Q(PC_2_q), .clk(clock_4_out), .clr(undriven_26));  // open: en
  Register #(.width(16)) DR_3 (.D(DR_3_q), .Q(DR_3_q), .clk(clock_4_out), .clr(undriven_27));  // open: en
  Register #(.width(16)) AC_2 (.D(undriven_24), .en(or_3_out), .Q(DR_3_q), .clk(clock_4_out), .clr(CLR_out));
  Register INPR_3 (.D(undriven_23));  // open: en, Q, clk, clr
  Register #(.width(16)) IR_3 (.D(DR_3_q), .Q(DR_3_q), .clk(clock_4_out));  // open: en, clr
  Register #(.width(16)) TR_2 (.D(DR_3_q), .Q(DR_3_q), .clk(clock_4_out), .clr(undriven_28));  // open: en
  Register OUTR_5 (.D(bit_extender_3_out), .clk(clock_4_out), .clr(undriven_29));  // open: en, Q
  Multiplexer #(.select(3), .width(16)) multiplexer_3 (
    .out(DR_3_q), .sel(in_6), .en(in_7));  // open: in0, in1, in2, in3, in4, in5, in6, in7
  RAM #(.addrWidth(12), .dataWidth(16), .bus("separate")) ram_3 (
    .addr(AR_3_q), .din(DR_3_q), .data(DR_3_q), .str(not_2_out), .clk(clock_4_out), .ld(in_9), .clr(in_8));  // open: sel
  assign DR_3_q = {{4{1'b0}}, AR_3_q};  // Bit_Extender bit_extender_4
  assign DR_3_q = {{4{1'b0}}, PC_2_q};  // Bit_Extender bit_extender_5
  Clock clock_4 (.out(clock_4_out));

  // Notes on the sheet:
  //   TO ALU
  //   NAND   1
  //   16 BIT ALU
  //   NOT   0
  //   DIV  2
  //   MUL  3
  //   SUC  4
  //   SUB  5
  //   ADC  6
  //   ADD  7
  //   NOT
  //   NAND
  //   DIV
  //   MUL
  //   SUC
  //   SUB
  //   ADC
  //   ADD
  //   D0
  //   T5
  //   D1
  //   T5
  //   D2
  //   T5
  //   P
  //   B11
  //   r
  //   B9
  //   B7
  //   B6
  //   B5
  //   B11
  //   TO AC
  //   LD
  //   INR
  //   CLR
  //   TO ALU
endmodule
