// Logisim project common bus system of NISUMANO.circ as structural Verilog: 1 circuit, main circuit main
module main (
  input  [2:0] in_1,
  input  in_2,
  input  in_3,
  input  in_4
);

  wire clock_1_out, not_1_out, undriven_3, undriven_4, undriven_5, undriven_6, undriven_7, undriven_8;
  wire [7:0] bit_extender_3_out, undriven;
  wire [11:0] AR_q, bit_extender_1_out, bit_extender_2_out, PC_q;
  wire [15:0] DR_q, undriven_2;

  not not_1 (not_1_out, in_4);
  Bit_Extender #(.in_width(16), .out_width(12)) bit_extender_1 (.in(DR_q), .out(bit_extender_1_out));
  Bit_Extender #(.in_width(16), .out_width(12)) bit_extender_2 (.in(DR_q), .out(bit_extender_2_out));
  Bit_Extender #(.in_width(16), .out_width(8)) bit_extender_3 (.in(DR_q), .out(bit_extender_3_out));
  Register #(.width(12)) AR (.D(bit_extender_1_out), .Q(AR_q), .clk(clock_1_out), .clr(undriven_3));  // open: en
  Register #(.width(12)) PC (.D(bit_extender_2_out), .Q(PC_q), .clk(clock_1_out), .clr(undriven_4));  // open: en
  Register #(.width(16)) DR (.D(DR_q), .Q(DR_q), .clk(clock_1_out), .clr(undriven_5));  // open: en
  Register #(.width(16)) AC (.D(undriven_2), .Q(DR_q), .clk(clock_1_out), .clr(undriven_6));  // open: en
  Register INPR (.D(undriven));  // open: en, Q, clk, clr
  Register #(.width(16)) IR (.D(DR_q), .Q(DR_q), .clk(clock_1_out));  // open: en, clr
  Register #(.width(16)) TR (.D(DR_q), .Q(DR_q), .clk(clock_1_out), .clr(undriven_7));  // open: en
  Register OUTR (.D(bit_extender_3_out), .clk(clock_1_out), .clr(undriven_8));  // open: en, Q
  Multiplexer #(.select(3), .width(16)) multiplexer_1 (
    .out(DR_q), .sel(in_1), .en(in_2));  // open: in0, in1, in2, in3, in4, in5, in6, in7
  RAM #(.addrWidth(12), .dataWidth(16), .bus("separate")) ram_1 (
    .addr(AR_q), .din(DR_q), .data(DR_q), .str(not_1_out), .clk(clock_1_out), .ld(in_4), .clr(in_3));  // open: sel
  assign DR_q = {{4{1'b0}}, AR_q};  // Bit_Extender bit_extender_4
  assign DR_q = {{4{1'b0}}, PC_q};  // Bit_Extender bit_extender_5
  Clock clock_1 (.out(clock_1_out));

  // Notes on the sheet:
  //   TO ALU
  //   common bus system 
endmodule
