// Logisim project control of AC.circ as structural Verilog: 1 circuit, main circuit main
module main (
  input  [3:0] in_1,
  output [2:0] out_2
);

  wire ADD_out, adder_1_cout, AND_out, CLR_out, COM_out, DR_out, INC_out, INPR_out, or_1_out, SHL_out,
       SHR_out, undriven, undriven_2, undriven_3, undriven_4, undriven_5, undriven_6, undriven_7, undriven_8,
       undriven_9, undriven_10, undriven_11, undriven_12, undriven_13, undriven_14, undriven_15, undriven_16,
       undriven_17, undriven_18, undriven_22;
  wire [2:0] bitfinder_1_index;
  wire [7:0] adder_1_out, undriven_19, undriven_20, undriven_21;

  and AND (AND_out, undriven, undriven_2);
  and ADD (ADD_out, undriven_3, undriven_4);
  and DR (DR_out, undriven_5, undriven_6);
  and INPR (INPR_out, undriven_7, undriven_8);
  and COM (COM_out, undriven_9, undriven_10);
  and SHR (SHR_out, undriven_11, undriven_12);
  and SHL (SHL_out, undriven_13, undriven_14);
  and INC (INC_out, undriven_15, undriven_16);
  and CLR (CLR_out, undriven_17, undriven_18);
  or or_1 (or_1_out, AND_out, ADD_out, DR_out, INPR_out, COM_out, SHR_out, SHL_out);
  BitAdder #(.width(4)) bitadder_1 (.in0(in_1), .out(out_2));
  BitFinder bitfinder_1 (.in(undriven_19), .index(bitfinder_1_index));  // open: found
  Adder adder_1 (.a(undriven_20), .b(undriven_21), .out(adder_1_out), .cin(undriven_22), .cout(adder_1_cout));

  // Notes on the sheet:
  //   D0
  //   T5
  //   D1
  //   T5
  //   D2
  //   T5
  //   P
  //   B11
  //   r
  //   B9
  //   B7
  //   B6
  //   B5
  //   B11
  //   TO AC
  //   LD
  //   INR
  //   CLR
endmodule
