// Logisim project sign.circ as structural Verilog: 1 circuit, main circuit main
// adder 1
module main (
  input  B3,
  input  B2,
  input  in_3,
  input  B1,
  input  B0,
  input  ADD_SUB,
  input  As,
  input  A3,
  input  A2,
  input  A1,
  input  A0,
  input  in_12,
  output MODE,
  output C3,
  output out_15,
  output C2,
  output out_17,
  output C1,
  output out_19,
  output out_20,
  output C0,
  output out_22
);

  wire adder_1_cout, adder_2_cout, adder_3_cout, adder_5_cout, adder_5_out, adder_6_cout, adder_6_out,
       adder_7_cout, adder_7_out, adder_8_cout, adder_8_out, and_1_out, and_2_out, not_1_out, not_2_out,
       not_3_out, not_4_out, not_5_out, not_6_out, not_7_out, or_2_out, xor_1_out, xor_2_out, xor_3_out,
       xor_4_out, xor_5_out;

  xor xor_1 (xor_1_out, B0, MODE);
  xor xor_2 (xor_2_out, in_3, MODE);
  xor xor_3 (xor_3_out, B1, MODE);
  xor xor_4 (xor_4_out, B3, As);
  not not_1 (not_1_out, xor_4_out);
  and and_1 (and_1_out, ADD_SUB, not_1_out);
  or or_1 (MODE, and_1_out, and_2_out);
  xor xor_5 (xor_5_out, B2, MODE);
  not not_2 (not_2_out, ADD_SUB);
  and and_2 (and_2_out, xor_4_out, not_2_out);
  Adder #(.width(1)) adder_1 (.a(xor_5_out), .b(A3), .out(out_15), .cin(MODE), .cout(adder_1_cout));
  Adder #(.width(1)) adder_2 (.a(xor_2_out), .b(A2), .out(out_17), .cin(adder_1_cout), .cout(adder_2_cout));
  Adder #(.width(1)) adder_3 (.a(xor_3_out), .b(A1), .out(out_19), .cin(adder_2_cout), .cout(adder_3_cout));
  Adder #(.width(1)) adder_4 (.a(xor_1_out), .b(A0), .out(out_20), .cin(adder_3_cout), .cout(out_22));
  not not_3 (not_3_out, ADD_SUB);
  not not_4 (not_4_out, out_15);
  not not_5 (not_5_out, out_17);
  not not_6 (not_6_out, out_19);
  not not_7 (not_7_out, out_20);
  or or_2 (or_2_out, out_22, not_3_out);
  Adder #(.width(1)) adder_5 (.a(not_4_out), .b(1'b1), .out(adder_5_out), .cout(adder_5_cout));  // open: cin
  Adder #(.width(1)) adder_6 (.a(in_12), .b(not_5_out), .out(adder_6_out), .cin(adder_5_cout), .cout(adder_6_cout));
  Adder #(.width(1)) adder_7 (.a(not_6_out), .b(in_12), .out(adder_7_out), .cin(adder_6_cout), .cout(adder_7_cout));
  Adder #(.width(1)) adder_8 (.a(not_7_out), .b(in_12), .out(adder_8_out), .cin(adder_7_cout), .cout(adder_8_cout));
  Multiplexer #(.enable("false")) multiplexer_1 (.in0(adder_5_out), .in1(out_15), .out(C3), .sel(or_2_out));
  Multiplexer #(.enable("false")) multiplexer_2 (.in0(adder_6_out), .in1(out_17), .out(C2), .sel(or_2_out));
  Multiplexer #(.enable("false")) multiplexer_3 (.in0(adder_7_out), .in1(out_19), .out(C1), .sel(or_2_out));
  Multiplexer #(.enable("false")) multiplexer_4 (.in0(adder_8_out), .in1(out_20), .out(C0), .sel(or_2_out));

  // Notes on the sheet:
  //   Bs
  //   SIGN MAGNITUDE ADDITION\ SUBTRACTION 
endmodule
