// Logisim project signedmag.circ as structural Verilog: 1 circuit, main circuit main
module main (
  input  in_1,
  input  in_2,
  input  in_3,
  input  in_4,
  input  in_5,
  input  in_6,
  input  in_7,
  input  in_8,
  input  in_9,
  input  in_10,
  input  in_11
);

  wire and_1_out, and_2_out, and_3_out, and_4_out, not_1_out, not_2_out, xor_1_out;

  xor xor_1 (xor_1_out, in_1, in_7);
  not not_1 (not_1_out, xor_1_out);
  not not_2 (not_2_out, in_6);
  and and_1 (and_1_out, xor_1_out, not_2_out);
  and and_2 (and_2_out, not_1_out, not_2_out);
  and and_3 (and_3_out, xor_1_out, in_6);
  and and_4 (and_4_out, not_1_out, in_6);
endmodule
